// Logisim project hack.circ as structural Verilog
module alu (
  input  [15:0] x,
  input  [15:0] y,
  input  zx,
  input  nx,
  input  zy,
  input  ny,
  input  f,
  input  no,
  output [15:0] o,
  output zr,
  output ng
);

  wire or_1_out;
  wire [15:0] adder_1_out, and_1_out, multiplexer_1_out, multiplexer_2_out, multiplexer_3_out,
       multiplexer_4_out, multiplexer_5_out, not_1_out, not_2_out, not_3_out;

  Multiplexer #(.width(16)) multiplexer_1 (.in0(x), .in1({16{1'b0}}), .out(multiplexer_1_out), .sel(zx));
  Multiplexer #(.width(16)) multiplexer_2 (.in0(y), .in1({16{1'b0}}), .out(multiplexer_2_out), .sel(zy));
  assign not_1_out = ~multiplexer_1_out;  // NOT_Gate not_1, 16 bits wide
  Multiplexer #(.width(16)) multiplexer_3 (.in0(multiplexer_2_out), .in1(not_2_out), .out(multiplexer_3_out), .sel(ny));
  assign not_2_out = ~multiplexer_2_out;  // NOT_Gate not_2, 16 bits wide
  Multiplexer #(.width(16)) multiplexer_4 (.in0(multiplexer_1_out), .in1(not_1_out), .out(multiplexer_4_out), .sel(nx));
  Adder #(.width(16)) adder_1 (.a(multiplexer_4_out), .b(multiplexer_3_out), .out(adder_1_out));  // open: cin, cout
  assign and_1_out = multiplexer_4_out & multiplexer_3_out;  // AND_Gate and_1, 16 bits wide
  Multiplexer #(.width(16)) multiplexer_5 (.in0(and_1_out), .in1(adder_1_out), .out(multiplexer_5_out), .sel(f));
  Multiplexer #(.width(16)) multiplexer_6 (.in0(multiplexer_5_out), .in1(not_3_out), .out({ng, o[14:0]}), .sel(no));
  assign not_3_out = ~multiplexer_5_out;  // NOT_Gate not_3, 16 bits wide
  or or_1 (or_1_out, o[0], o[1], o[2], o[3], o[4], o[5], o[6], o[7], o[8], o[9], o[10], o[11], o[12], o[13], o[14], ng);
  not not_4 (zr, or_1_out);

  assign o[15] = ng;
endmodule

module cpu (
  input  [15:0] instr_bus,
  input  clk,
  input  [15:0] data_bus_in,
  input  reset,
  output [15:0] data_output_bus,
  output write_enable,
  output [14:0] data_address_bus,
  output [14:0] instruction_address_bus
);

  wire not_1_out;
  wire [15:0] A_q, multiplexer_1_out, multiplexer_2_out;

  Multiplexer #(.width(16)) multiplexer_1 (
    .in0(data_output_bus), .in1(instr_bus), .out(multiplexer_1_out), .sel(not_1_out));
  not not_1 (not_1_out, instr_bus[15]);
  Register #(.width(16)) D (.D(data_output_bus), .clk(clk));  // open: en, Q, clr
  Register #(.width(16)) A (.D(multiplexer_1_out), .en(not_1_out), .clk(clk), .Q(A_q));  // open: clr
  Multiplexer #(.width(16)) multiplexer_2 (.in0(A_q), .out(multiplexer_2_out));  // open: in1, sel
  alu alu_1 (.y(multiplexer_2_out), .o(data_output_bus));  // open: x, zx, nx, zy, ny, f, no, zr, ng
endmodule
