// Logisim project my_hack.circ as structural Verilog: 8 circuits, main circuit main
module main (
);

  wire button_2_out, clk, my_mux_a, my_mux_alu, my_w_a, my_w_d, my_w_pc, my_write_m, ng, zr;
  wire [14:0] A_q;
  wire [15:0] alu_1_o, D_q, instr, multiplexer_1_out, multiplexer_2_out, pc_q, ram_1_dout;
  wire [15:15] A_q_2;

  ROM #(.addrWidth(16), .dataWidth(16)) rom_1 (.addr(pc_q), .data(instr));
  Clock clock_1 (.out(clk));
  Button button_1 ();  // open: out
  Register #(.width(16)) A (.D(multiplexer_1_out), .en(my_w_a), .clk(clk), .Q({A_q_2[15], A_q}));  // open: clr
  Multiplexer #(.width(16)) multiplexer_1 (.in0(alu_1_o), .in1(instr), .out(multiplexer_1_out), .sel(my_mux_a));
  // Probe on ram_1_dout
  W_A w_a_1 (.in_1(instr), .w(my_w_a));
  MUX_A mux_a_1 (.instr(instr), .o(my_mux_a));
  W_D w_d_1 (.in_1(instr), .o(my_w_d));
  MUX_ALU mux_alu_1 (.in_1(instr), .o(my_mux_alu));
  write_M write_m_1 (.in_1(instr), .out_2(my_write_m));
  Register #(.width(16)) D (.D(alu_1_o), .en(my_w_d), .clk(clk), .Q(D_q));  // open: clr
  Multiplexer #(.width(16)) multiplexer_2 (
    .in0({A_q_2[15], A_q}), .in1(ram_1_dout), .out(multiplexer_2_out), .sel(my_mux_alu));
  Counter #(.max('hffff), .width(16)) pc (
    .load(my_w_pc), .D({A_q_2[15], A_q}), .Q(pc_q), .clk(clk), .clr(button_2_out));  // open: count, carry, up
  Button button_2 (.out(button_2_out));
  alu alu_1 (
    .x(D_q), .y(multiplexer_2_out), .zx(instr[11]), .nx(instr[10]), .zy(instr[9]), .ny(instr[8]),
    .f(instr[7]), .no(instr[6]), .o(alu_1_o), .zr(zr), .ng(ng));
  W_PC w_pc_1 (.in_1(instr), .zr(zr), .ng(ng), .o(my_w_pc));
  RAM #(.addrWidth(15), .dataWidth(16)) ram_1 (
    .addr(A_q), .we(my_write_m), .oe(1'b1), .clk(clk), .din(alu_1_o), .dout(ram_1_dout));

  // Notes on the sheet:
  //   contents of rom_1 (hex, n*v repeats v):
  //   5 ec10 3 e090 8 e302 a ea88 8 1 ec10 0 e308 4 ec10 4 e090 10 e302 12 ea88 10 1 ec10 1 e308 6 ec10 4
  //   e090 18 e306 1a ea88 18 1 ec10 2 e308 2 ec10 7 e090 20 e304 22 ea88 20 1 ec10 3 e308 8 ec10 9 e090
  //   28 e301 2a ea88 28 1 ec10 4 e308 4 ec10 4 e090 30 e303 32 ea88 30 1 ec10 5 e308 32 ea87
  //   CPU
endmodule

module alu (
  input  [15:0] x,
  input  [15:0] y,
  input  zx,
  input  nx,
  input  zy,
  input  ny,
  input  f,
  input  no,
  output [15:0] o,
  output zr,
  output ng
);

  wire or_1_out;
  wire [15:0] adder_1_out, and_1_out, multiplexer_1_out, multiplexer_2_out, multiplexer_3_out,
       multiplexer_4_out, not_1_out, not_2_out;

  Multiplexer #(.width(16)) multiplexer_1 (.in0(x), .in1({16{1'b0}}), .out(multiplexer_1_out), .sel(zx));
  Multiplexer #(.width(16)) multiplexer_2 (.in0(y), .in1({16{1'b0}}), .out(multiplexer_2_out), .sel(zy));
  assign not_1_out = ~multiplexer_1_out;  // NOT_Gate not_1, 16 bits wide
  assign not_2_out = ~multiplexer_2_out;  // NOT_Gate not_2, 16 bits wide
  Multiplexer #(.width(16)) multiplexer_3 (.in0(multiplexer_1_out), .in1(not_1_out), .out(multiplexer_3_out), .sel(nx));
  Multiplexer #(.width(16)) multiplexer_4 (.in0(multiplexer_2_out), .in1(not_2_out), .out(multiplexer_4_out), .sel(ny));
  assign and_1_out = multiplexer_3_out & multiplexer_4_out;  // AND_Gate and_1, 16 bits wide
  Adder #(.width(16)) adder_1 (.a(multiplexer_3_out), .b(multiplexer_4_out), .out(adder_1_out));  // open: cin, cout
  Multiplexer #(.width(16)) multiplexer_5 (.in0(and_1_out), .in1(adder_1_out), .out({ng, o[14:0]}), .sel(f));
  or or_1 (or_1_out, o[0], o[1], o[2], o[3], o[4], o[5], o[6], o[7], o[8], o[9], o[10], o[11], o[12], o[13], o[14], ng);
  not not_3 (zr, or_1_out);

  assign o[15] = ng;
endmodule

module W_A (
  input  [15:0] in_1,
  output w
);

  not not_1 (w, in_1[15]);
endmodule

module MUX_A (
  input  [15:0] instr,
  output o
);

  not not_1 (o, instr[15]);
endmodule

module W_D (
  input  [15:0] in_1,
  output o
);

  and and_1 (o, in_1[15], in_1[4]);
endmodule

module MUX_ALU (
  input  [15:0] in_1,
  output o
);

  and and_1 (o, in_1[15], in_1[12]);
endmodule

module write_M (
  input  [15:0] in_1,
  output out_2
);

  and and_1 (out_2, in_1[15], in_1[3]);
endmodule

module W_PC (
  input  [15:0] in_1,
  input  zr,
  input  ng,
  output o
);

  wire and_1_out, and_2_out, JEQ_out, JGE_out, JGT_out, JLE_out, JLT_out, JMP_out, JNE_out, not_1_out,
       not_2_out, not_3_out, not_4_out, not_5_out, not_6_out, not_7_out, not_8_out, not_9_out, not_10_out,
       not_11_out, not_12_out, not_13_out, not_14_out, not_15_out, or_1_out, or_2_out, or_3_out;

  not not_1 (not_1_out, zr);
  not not_2 (not_2_out, ng);
  and and_1 (and_1_out, not_1_out, not_2_out);
  not not_3 (not_3_out, in_1[2]);
  not not_4 (not_4_out, in_1[1]);
  not not_5 (not_5_out, zr);
  not not_6 (not_6_out, ng);
  not not_7 (not_7_out, in_1[2]);
  not not_8 (not_8_out, in_1[0]);
  not not_9 (not_9_out, in_1[2]);
  or or_1 (or_1_out, and_1_out, zr);
  and JGT (JGT_out, not_3_out, not_4_out, in_1[0], not_5_out, not_6_out);
  and JEQ (JEQ_out, not_7_out, in_1[1], not_8_out, zr);
  and JGE (JGE_out, not_9_out, in_1[1], in_1[0], or_1_out);
  not not_10 (not_10_out, zr);
  and and_2 (and_2_out, ng, not_10_out);
  not not_11 (not_11_out, in_1[1]);
  not not_12 (not_12_out, in_1[0]);
  not not_13 (not_13_out, in_1[1]);
  not not_14 (not_14_out, zr);
  not not_15 (not_15_out, in_1[0]);
  or or_2 (or_2_out, zr, and_2_out);
  and JNE (JNE_out, in_1[2], not_13_out, in_1[0], not_14_out);
  and JLE (JLE_out, in_1[2], in_1[1], not_15_out, or_2_out);
  and JLT (JLT_out, in_1[2], not_11_out, not_12_out, ng);
  and JMP (JMP_out, in_1[2], in_1[1], in_1[0]);
  or or_3 (or_3_out, JGT_out, JLT_out, JEQ_out, JNE_out, JGE_out, JLE_out, JMP_out);
  and and_3 (o, in_1[15], or_3_out);

  // Other names for the same wires on the sheet: j3 = in_1[0]; j2 = in_1[1]; j1 = in_1[2]
endmodule
